# Fritzing sketch schema (saved by Fritzing 0.9.10b)
breadboards: 1

parts:
  Composant1 = Arduino Mega 2560 (Rev3)
  microSD1 = MicroSD Card Module
  LCD2004-I2C1 = LCD2004-I2C
  S1 = Pushbutton [package="[THT]"]
  S2 = Pushbutton [package="[THT]"]
  S3 = Pushbutton [package="[THT]"]
  S4 = Pushbutton [package="[THT]"]
  Composant2 = HX711 Weighing Sensor Module  # not connected
  S5 = Load Sensor - 50kg [part_number=SEN-10245]  # not connected
  S6 = Load Sensor - 50kg [part_number=SEN-10245]  # not connected
  S7 = Load Sensor - 50kg [part_number=SEN-10245]  # not connected
  S8 = Load Sensor - 50kg [part_number=SEN-10245]  # not connected

nets:
  N1: Composant1.D21/SCL, LCD2004-I2C1.SCL
  N2: Composant1.D20/SDA, LCD2004-I2C1.SDA
  VCC: Composant1.5V, microSD1.VCC, LCD2004-I2C1.VCC
  GND: Composant1.GND, microSD1.GND, LCD2004-I2C1.GND
  N3: S1.Pin_1, S1.Pin_2
  N4: S1.Pin_3, S1.Pin_4
  N5: S2.Pin_1, S2.Pin_2
  N6: S2.Pin_3, S2.Pin_4
  N7: S3.Pin_1, S3.Pin_2
  N8: S3.Pin_3, S3.Pin_4
  N9: S4.Pin_1, S4.Pin_2
  N10: S4.Pin_3, S4.Pin_4

custom parts:
  LCD2004-I2C: A standard character display with 4x20 characters. Comes in many colors with LCM2004 IIC attached.
  Load Sensor - 50kg: Half-wheatstone bridge Load Cell modified from the Fritzing Repo This load sensor, sometimes called a strain gauge, is the same one found in digital bathroom scales (you know, the ones you use in January for your New Year's resolutions, and then forget about a month later). This sensor can measure up to about 110 pounds.
